# Fritzing sketch Scheme (saved by Fritzing 1.0.3b)

parts:
  esp1 = ESP32 DevKitc V4
  Part1 = Adafruit TCA9548A
  DHT1 = Humidity and Temperature Sensor DHT11
  M1 = HTU21d
  M2 = HTU21d
  M3 = HTU21d
  LCD1 = LCD screen
  R1 = Resistor [tolerance=±5% resistance=1k package="2512 [SMD]"]
  R2 = Resistor [tolerance=±5% resistance=2.2k package="2512 [SMD]"]
  R3 = Resistor [tolerance=±5% resistance=10k package="2010 [SMD]"]  # not connected

nets:
  N1: esp1.IO15, DHT1.Data-signal
  N2: esp1.IO18, LCD1.DB6
  N3: esp1.IO19, LCD1.DB7
  N4: esp1.IO21, Part1.INPUTSDA
  N5: esp1.IO22, Part1.INPUTSCL
  GND: esp1.GND, Part1.GND
  N6: esp1.IO32, LCD1.DB5
  N7: esp1.IO33, LCD1.DB4
  N8: esp1.IO25, LCD1.E
  N9: esp1.IO26, LCD1.RS
  5V: esp1.5V, Part1.VCC
  N10: Part1.2SDA, M3.SDA
  N11: Part1.2SCL, M3.SCL
  N12: Part1.0SDA, M1.SDA
  N13: Part1.0SCL, M1.SCL
  N14: Part1.1SDA, M2.SDA
  N15: Part1.1SCL, M2.SCL
  N16: LCD1.V0, R2.Pin_0
  N17: LCD1.LED+, R1.Pin_0

notes:
  10K
  1K
  2.2K
  E->25
  RS->26
  D4->33
  D5->32
  D6->18
  D7->19
  15
  21
  22

custom parts:
  ESP32 DevKitc V4: ESP32-DevKitC board with ESP32-WROOM-32 module. ESP32-DevKitC V4 is a small-sized ESP32-based development board produced by Espressif. Most of the pins on the ESP module are broken out to the pin headers on the board. The pins D0, D1, D2, D3, CMD and CLK are used internally for communication between ESP32 and SPI flash memory. They are grouped on both sides near the USB connector. Avoid using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
  Adafruit TCA9548A: You just found the perfect I2C sensor, and you want to wire up two or three or more of them to your Arduino when you realize "Uh oh, this chip has a fixed I2C address, and from what I know about I2C, you cannot have two devices with the same address on the same SDA/SCL pins!" Are you out of luck? You would be, if you didn't have this ultra-cool TCA9548A 1-to-8 I2C multiplexer! Finally, a way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
  Humidity and Temperature Sensor DHT11: Digital relative humidity & temperature sensor DHT11
  HTU21d: Temperature Humidity Sensor, I2C
